# Fritzing sketch knocklock (saved by Fritzing 0.9.0b)

parts:
  Часть1 = Troyka Shield
  Часть2 = Troyka Button
  Часть3 = Troyka Buzzer
  Часть4 = Troyka Led
  Часть5 = Troyka Potentiometer
  J1 = Basic Servo
  Часть6 = Arduino Uno (Rev3)  # not connected

nets:
  N1: Часть1.D3, Часть4.S
  N2: Часть1.D4, Часть3.S
  N3: Часть1.D5, Часть2.S
  N4: Часть1.D6, J1.pulse
  N5: Часть1.VCC3, Часть4.V
  N6: Часть1.VCC4, Часть3.V
  N7: Часть1.VCC5, Часть2.V
  N8: Часть1.VCC6, J1.vcc
  N9: Часть1.GND3, Часть4.G
  N10: Часть1.GND4, Часть3.G
  N11: Часть1.GND5, Часть2.G
  GND6: Часть1.GND6, J1.gnd
  N12: Часть1.SIG_A1, Часть5.S
  N13: Часть1.VCC1, Часть5.V
  N14: Часть1.GND1, Часть5.G
